# Fritzing sketch datalogger (saved by Fritzing 0.5.2b)
breadboards: 1

parts:
  J1 = Infrared Proximity Sensor
  J2 = Infrared Proximity Sensor
  Arduino1 = Arduino
  R1 = Photocell (LDR) [package=THT]
  R2 = Resistor [resistance=10k package=THT]
  R3 = Resistor [resistance=10k package=THT]
  R4 = Resistor [resistance=10k package=THT]
  Arduino_micro_SD_module1 = Arduino_microsd
  U1 = mystery part, 5 pins [chip_label=TC74A0 spacing=300mil]

nets (from the breadboard view):
  N1: J1.Vout, Arduino1.A3
  GND: J1.GND, J2.GND, Arduino1.GND, R2.Pin_0, Arduino_micro_SD_module1.connector0, U1.pin3
  VCC: J1.Vcc, J2.Vcc, Arduino1.+5V, R1.pin_0, R3.Pin_1, R4.Pin_1, U1.pin5
  N2: J2.Vout, Arduino1.A2
  N3: Arduino1.D13, Arduino_micro_SD_module1.connector1
  N4: Arduino1.D12, Arduino_micro_SD_module1.connector2
  N5: Arduino1.D11, Arduino_micro_SD_module1.connector3
  N6: Arduino1.D10, Arduino_micro_SD_module1.connector4
  N7: Arduino1.D9, Arduino_micro_SD_module1.connector5
  N8: Arduino1.D8, Arduino_micro_SD_module1.connector6
  N9: Arduino1.A1, R1.pin_1, R2.Pin_1
  N10: Arduino1.A4, R3.Pin_0, U1.pin2
  N11: Arduino1.A5, R4.Pin_0, U1.pin4
