# Fritzing sketch security (saved by Fritzing 0.5.2b)
breadboards: 1

parts:
  R4 = Resistor [resistance=1k package=THT]
  Arduino2 = Arduino Mega
  Arduino_RFID_125_kHz1 = Arduino_rfid
  RFID_antenna_125_kHz1 = RFID_antenna
  LED1 = Red LED - 5mm [package="5 mm [THT]"]
  SPKR1 = Loudspeaker
  S1 = Pushbutton [package="[THT]"]
  R3 = Resistor [resistance=100 package=THT]
  J1 = Basic Servo
  R3_2 = Resistor [resistance=100 package=THT]

nets:
  N1: R4.Pin_0, Arduino_RFID_125_kHz1.connector4, S1.Pin_1, S1.Pin_2, R3.Pin_0
  5V: R4.Pin_1, Arduino2.+5V, J1.vcc
  N2: Arduino2.D9, J1.pulse
  N3: Arduino2.D8, R3_2.Pin_0
  GND: Arduino2.GND, LED1.cathode, SPKR1.pin1, S1.Pin_3, S1.Pin_4, J1.gnd
  N4: Arduino_RFID_125_kHz1.connector20, RFID_antenna_125_kHz1.connector1
  N5: Arduino_RFID_125_kHz1.connector21, RFID_antenna_125_kHz1.connector0
  N6: LED1.anode, R3.Pin_1
  N7: SPKR1.pin2, R3_2.Pin_1
