# Fritzing sketch LCD and temperature (saved by Fritzing 0.6.2b)
breadboards: 1

parts:
  Arduino1 = Arduino [part_number=Uno]
  U1 = mystery part, 5 pins [chip_label=TC74 spacing=300mil part_number=TC74]
  LCD1 = LCD screen
  R2 = Resistor [tolerance=±5% resistance=10k power=25W package=THT]
  R3 = Resistor [tolerance=±5% resistance=10k power=25W package=THT]
  S1 = Pushbutton [package="[THT]"]
  R4 = Trimmer Potentiometer [maximum_resistance=10kΩ package=THT]
  R5 = Resistor [tolerance=±5% resistance=10k power=25W package=THT]

nets:
  GND: Arduino1.GND, U1.pin3, LCD1.VSS, LCD1.R/W, LCD1.LED-, R4.leg1, R5.Pin_1
  N1: Arduino1.D8, S1.Pin_3, S1.Pin_4, R5.Pin_0
  N2: Arduino1.D7, LCD1.DB7
  N3: Arduino1.D6, LCD1.DB6
  N4: Arduino1.D5, LCD1.DB5
  N5: Arduino1.D4, LCD1.DB4
  N6: Arduino1.D3, LCD1.E
  N7: Arduino1.D2, LCD1.RS
  +5V: Arduino1.+5V, U1.pin5, LCD1.VDD, LCD1.LED+, R2.Pin_1, R3.Pin_1, S1.Pin_1, S1.Pin_2, R4.leg2
  N8: Arduino1.A4, U1.pin2, R3.Pin_0
  N9: Arduino1.A5, U1.pin4, R2.Pin_0
  N10: LCD1.V0, R4.wiper
