# Fritzing sketch Holiday Lights (saved by Fritzing 0.6.2b)
breadboards: 1

parts:
  Arduino1 = Arduino [part_number=Uno]
  R4 = Trimmer Potentiometer [maximum_resistance=10kΩ package=THT]
  R5 = Trimmer Potentiometer [maximum_resistance=10kΩ package=THT]
  R6 = Resistor [tolerance=±5% resistance=100 package=THT]
  R7 = Resistor [tolerance=±5% resistance=100 package=THT]
  TRS1 = Stereo Jack (TRS) 3.5mm [package="PG203J [THT]"]
  LED1 = Red LED - 5mm [package="5 mm [THT]"]
  LED2 = green LED - 5mm [package="5 mm [THT]"]
  R8 = Resistor [tolerance=±5% resistance=220 package=THT]
  R9 = Resistor [tolerance=±5% resistance=220 package=THT]
  IC1 = IC, DIP package, 14 pins [chip_label=LM324 spacing=300mil]
  R10 = Resistor [tolerance=±5% resistance=10k package=THT]
  R11 = Resistor [tolerance=±5% resistance=10k package=THT]
  C1 = Electrolytic Capacitor [capacitance=10µF voltage=10V package="100 mil [THT, electrolytic]"]
  C2 = Electrolytic Capacitor [capacitance=10µF voltage=10V package="100 mil [THT, electrolytic]"]
  J1 = screw terminal, 4 pins
  Power_plug1 = Power plug
  U1 = mystery part, 4 pins [chip_label=LIGHTS spacing=300mil]

nets:
  GND: Arduino1.GND, R6.Pin_0, R7.Pin_0, TRS1.Sleeve, R8.Pin_1, R9.Pin_1, IC1.pin11, R10.Pin_1, R11.Pin_1, C1.-, C2.-, J1.pin1, Power_plug1.GND, U1.pin4
  N1: Arduino1.D3, J1.pin4, U1.pin1
  N2: Arduino1.D2, J1.pin3, U1.pin2
  N3: Arduino1.+5V, IC1.pin4
  N4: Arduino1.A0, LED2.anode, IC1.pin6, IC1.pin7, R11.Pin_0, C2.+
  N5: Arduino1.A1, LED1.anode, IC1.pin8, IC1.pin9, R10.Pin_0, C1.+
  N6: R4.wiper, IC1.pin1, IC1.pin5
  N7: R4.leg2, R6.Pin_1, IC1.pin2
  N8: R5.wiper, IC1.pin10, IC1.pin14
  N9: R5.leg2, R7.Pin_1, IC1.pin13
  N10: TRS1.Ring, IC1.pin3
  N11: TRS1.Tip, IC1.pin12
  N12: LED1.cathode, R8.Pin_0
  N13: LED2.cathode, R9.Pin_0
  N14: J1.pin2, Power_plug1.VCC, U1.pin3
