# Fritzing sketch GPS (saved by Fritzing 0.7.5b)

parts:
  Arduino_GPS_module1 = Arduino_GPS_module
  Arduino_micro_SD_module1 = Arduino_microsd
  VCC1 = Battery block 9V
  Arduino1 = Arduino Mega [part_number=2560]
  S1 = Toggle Switch [package=THT]

nets:
  N1: Arduino_GPS_module1.aún_sin_nombre#connector5V1, Arduino_micro_SD_module1.aún_sin_nombre#17, Arduino1.+5V
  N2: Arduino_GPS_module1.aún_sin_nombre#connectorGND1, Arduino_micro_SD_module1.aún_sin_nombre#21, VCC1.-, Arduino1.GND
  N3: Arduino_GPS_module1.aún_sin_nombre#connectord0, Arduino1.D14
  N4: Arduino_GPS_module1.aún_sin_nombre#connectord1, Arduino1.D15
  N5: Arduino_GPS_module1.aún_sin_nombre#connectord2, Arduino1.D16
  N6: Arduino_GPS_module1.aún_sin_nombre#connectord3, Arduino1.D17
  N7: Arduino_GPS_module1.aún_sin_nombre#connectord4, Arduino1.D18
  N8: Arduino_GPS_module1.aún_sin_nombre#connectord5, Arduino1.D19
  N9: Arduino_GPS_module1.aún_sin_nombre#connectord6, Arduino1.D20
  N10: Arduino_GPS_module1.aún_sin_nombre#connectord7, Arduino1.D21
  N11: Arduino_micro_SD_module1.aún_sin_nombre#16, Arduino1.D50
  N12: Arduino_micro_SD_module1.aún_sin_nombre#18, Arduino1.D52
  N13: Arduino_micro_SD_module1.aún_sin_nombre#19, Arduino1.D51
  N14: Arduino_micro_SD_module1.aún_sin_nombre#20, Arduino1.RST
  N15: Arduino_micro_SD_module1.aún_sin_nombre#22, Arduino1.D11
  N16: Arduino_micro_SD_module1.aún_sin_nombre#23, Arduino1.D53
  N17: VCC1.+, S1.COM
  N18: Arduino1.VIN, S1.L2

custom parts:
  Arduino_GPS_module: Arduino GPS Module is a small electronic circuit that allows to connect to your Arduino board to get position and altitude, as well as speed, date and time on UTC (Universal Time Coordinated)
  Arduino_microsd: Arduino MicroSD module is a small shield that you can connect to your Arduino board, once the shield is connected, you add SD flash memory to Arduino.
